# Fritzing sketch programming_esp8266 (saved by Fritzing 0.9.3b)
breadboards: 1

parts:
  01 = ESP8266 WiFi Module [part_number=ESP8266]
  Breadboard_Power_Supply = YwRobot Breadboard Power Supply [part_number=545043]
  FT232RL_Programmer = FTDI Basic Programmer

nets:
  N1: 01.RXD, FT232RL_Programmer.TXO
  N2: 01.VCC, 01.GPIO_0, 01.GPIO_2, 01.CH_PD, Breadboard_Power_Supply.VCC#9, Breadboard_Power_Supply.VCC#10
  GND: 01.GND, Breadboard_Power_Supply.GND#13, Breadboard_Power_Supply.GND#14, FT232RL_Programmer.GND
  N3: 01.TXD, FT232RL_Programmer.RXI
  N4: Breadboard_Power_Supply.VCC#5, Breadboard_Power_Supply.VCC#6
  N5: Breadboard_Power_Supply.GND#11, Breadboard_Power_Supply.GND#12

custom parts:
  ESP8266 WiFi Module: Generic WiFi Module based on the ESP8266 with onboard PCB antenna and UART communications
  YwRobot Breadboard Power Supply: The YwRobot Breadboard Power Supply (MB-V2) has two power rails; they can be 5V or 3V3. Power to the module can be provided through the female USB socket or through the A10 (female) 2.1mm power jack.
