# Fritzing sketch roomba_esp8266 (saved by Fritzing 0.9.3b)

parts:
  01 = ESP8266 WiFi Module [part_number=ESP8266]
  Roomba_Din = DIN7 [package=din7]
  Buck_Converter_3_3V = RioRand LM2596
  PNP_Transistor = PNP-Transistor [package="TO92 [THT]"]

nets:
  N1: 01.RXD, PNP_Transistor.C
  N2: 01.VCC, 01.CH_PD, Buck_Converter_3_3V.Pin_3
  N3: 01.GND, Buck_Converter_3_3V.Pin_4, PNP_Transistor.E
  N4: 01.TXD, Roomba_Din.3
  N5: Roomba_Din.2, Buck_Converter_3_3V.Pin_1
  N6: Roomba_Din.4, PNP_Transistor.B
  N7: Roomba_Din.6, Buck_Converter_3_3V.Pin_2

custom parts:
  ESP8266 WiFi Module: Generic WiFi Module based on the ESP8266 with onboard PCB antenna and UART communications
